// Logisim project 2s_complement.circ as structural Verilog: 1 circuit, main circuit main
module main (
  input  [3:0] _4_bits,
  input  [3:0] _1s_complement,
  input  add_prime_sub,
  output [3:0] out_4
);

  wire [3:0] multiplexer_1_out, not_1_out;

  assign not_1_out = ~_4_bits;  // NOT_Gate not_1, 4 bits wide
  Multiplexer #(.width(4), .enable("false")) multiplexer_1 (
    .in0(_4_bits), .in1(not_1_out), .out(multiplexer_1_out), .sel(add_prime_sub));
  Adder #(.width(4)) adder_1 (.a(multiplexer_1_out), .b(_1s_complement), .out(out_4));  // open: cin, cout

  // Notes on the sheet:
  //   4 bits
  //   4 bits
endmodule
