// Logisim project 3_bit_counter.circ as structural Verilog: 1 circuit, main circuit main
module main (
  input  in_1,
  input  in_2,
  input  [2:0] INPUT,
  input  [2:0] plus_1,
  input  [2:0] minus_1,
  input  [2:0] _0,
  input  [1:0] in_7,
  output [2:0] Counter_out
);

  wire clock_1_out;
  wire [2:0] multiplexer_1_out, multiplexer_2_out, register_1_q;

  Register #(.width(3)) register_1 (.D(Counter_out), .en(in_1), .clk(clock_1_out), .Q(register_1_q));  // open: clr
  Clock clock_1 (.out(clock_1_out));
  Multiplexer #(.width(3), .enable("false")) multiplexer_1 (
    .in0(register_1_q), .in1(INPUT), .out(multiplexer_1_out), .sel(in_2));
  Multiplexer #(.select(2), .width(3), .enable("false")) multiplexer_2 (
    .in1(plus_1), .in2(minus_1), .in3(_0), .out(multiplexer_2_out), .sel(in_7));  // open: in0
  Adder #(.width(3)) adder_1 (.a(multiplexer_1_out), .b(multiplexer_2_out), .out(Counter_out));  // open: cin, cout
endmodule
