// Logisim project ALU.circ as structural Verilog: 1 circuit, main circuit main
module main (
  input  mode,
  input  in_2,
  input  in_3,
  input  [3:0] A,
  input  [3:0] B,
  output [3:0] ALUout
);

  wire [3:0] adder_1_out, and_1_out, multiplexer_1_out, multiplexer_2_out, multiplexer_3_out, nor_1_out,
       not_1_out;

  assign not_1_out = ~B;  // NOT_Gate not_1, 4 bits wide
  Multiplexer #(.width(4), .enable("false")) multiplexer_1 (
    .in0(B), .in1(not_1_out), .out(multiplexer_1_out), .sel(in_3));
  assign and_1_out = A & B;  // AND_Gate and_1, 4 bits wide
  Multiplexer #(.width(4), .enable("false")) multiplexer_2 (
    .in0(and_1_out), .in1(nor_1_out), .out(multiplexer_2_out), .sel(in_3));
  assign nor_1_out = ~(A | B);  // NOR_Gate nor_1, 4 bits wide
  Adder #(.width(4)) adder_1 (.a(A), .b(multiplexer_1_out), .out(adder_1_out), .cin(in_3));  // open: cout
  Multiplexer #(.width(4), .enable("false")) multiplexer_3 (
    .in0(adder_1_out), .in1(multiplexer_2_out), .out(multiplexer_3_out), .sel(in_2));
  Multiplexer #(.width(4), .enable("false")) multiplexer_4 (.in0(multiplexer_3_out), .in1(B), .out(ALUout), .sel(mode));

  // Notes on the sheet:
  //   Arithmetic Logic Unit (ALU)
  //   mode:
  //   000 -> ALUout = A+B (add)
  //   001 -> ALUout = A-B (sub)
  //   010 -> ALUout = A AND B (and)
  //   011 -> ALUout = A NOR B (nor)
  //   1xx -> ALUout = B (pass B)
endmodule
