// Logisim project analogy_1_to_1.circ as structural Verilog: 1 circuit, main circuit main
module main (
  input  in_1,
  input  Ad,
  input  Bd,
  output Ago,
  output Bgo
);

  wire and_1_out, and_2_out, and_3_out, clock_1_out, not_1_out, not_2_out, not_3_out, or_1_out, or_2_out,
       or_3_out, register_1_q;

  not not_1 (not_1_out, Ad);
  not not_2 (not_2_out, Bd);
  Clock clock_1 (.out(clock_1_out));
  Register #(.width(1)) register_1 (.D(or_1_out), .en(in_1), .clk(clock_1_out), .Q(register_1_q));  // open: clr
  and and_1 (and_1_out, not_1_out, register_1_q);
  not not_3 (not_3_out, register_1_q);
  and and_2 (and_2_out, Bd, not_3_out);
  and and_3 (and_3_out, not_3_out, not_2_out);
  or or_1 (or_1_out, and_2_out, and_1_out);
  or or_2 (or_2_out, register_1_q, and_3_out);
  or or_3 (or_3_out, not_3_out, not_1_out);
  and and_4 (Ago, Ad, or_2_out);
  and and_5 (Bgo, Bd, or_3_out);
endmodule
