// Logisim project decoder_2_to_4.circ as structural Verilog: 1 circuit, main circuit main
module main (
  input  in_1,
  input  in_2,
  output _00,
  output _01,
  output _10,
  output _11
);

  wire not_1_out, not_2_out;

  not not_1 (not_1_out, in_2);
  not not_2 (not_2_out, in_1);
  and and_1 (_00, not_1_out, not_2_out);
  and and_2 (_01, in_2, not_2_out);
  and and_3 (_10, not_1_out, in_1);
  and and_4 (_11, in_2, in_1);

  // Notes on the sheet:
  //   Make sure to Enable the Simulation (see menu)
  //   Reset simulation if it is not working properly
  //   Select the hand (upper left symbol OR Ctrl+1) to change input values
endmodule
