// Logisim project latches_RS_D.circ as structural Verilog: 1 circuit, main circuit main
module main (
  input  RESET,
  input  SET,
  input  DATA,
  input  LOAD,
  output OUTPUT,
  output NOT_OUTPUT,
  output OUTPUT_2,
  output NOT_OUTPUT_2
);

  wire and_1_out, and_2_out, not_1_out;

  not not_1 (not_1_out, DATA);
  nor nor_1 (OUTPUT, RESET, NOT_OUTPUT);
  nor nor_2 (NOT_OUTPUT, OUTPUT, SET);
  and and_1 (and_1_out, not_1_out, LOAD);
  and and_2 (and_2_out, DATA, LOAD);
  nor nor_3 (OUTPUT_2, and_1_out, NOT_OUTPUT_2);
  nor nor_4 (NOT_OUTPUT_2, OUTPUT_2, and_2_out);

  // Notes on the sheet:
  //   Ctrl+I -> step simulation
  //   Ctrl+R -> RESET simulation
  //   Ctrl+E -> Enable/disable simulation
  //   LATCH RS
  //   LATCH D
  //   RESET
  //   SET
endmodule
