// Logisim project master_slave_register.circ as structural Verilog: 1 circuit, main circuit main
module main (
  input  SET,
  input  RESET,
  input  in_3,
  input  in_4,
  input  in_5,
  output out_6
);

  wire clock_1_out, not_1_out, s_r_ff_1_q;

  S_R_Flip_Flop s_r_ff_1 (.S(SET), .R(RESET), .clk(not_1_out), .Q(s_r_ff_1_q), .reset(in_4));  // open: Qn, preset
  not not_1 (not_1_out, clock_1_out);
  S_R_Flip_Flop s_r_ff_2 (.S(s_r_ff_1_q), .R(in_3), .clk(clock_1_out), .Q(out_6), .reset(in_5));  // open: Qn, preset
  Clock clock_1 (.out(clock_1_out));

  // Notes on the sheet:
  //   Ctrl+K to start animation
  //   MASTER
  //   SLAVE
endmodule
