// Logisim project shift_register.circ as structural Verilog: 1 circuit, main circuit main
module main (
  input  in_1,
  input  in_2,
  output out_3,
  output SHIFT_REGISTER,
  output out_5,
  output out_6
);

  wire not_1_out;

  not not_1 (not_1_out, out_3);
  D_Flip_Flop d_ff_1 (.D(not_1_out), .clk(in_2), .Q(out_3));  // open: Qn, preset, reset
  D_Flip_Flop d_ff_2 (.D(out_3), .clk(in_1), .Q(SHIFT_REGISTER));  // open: Qn, preset, reset
  D_Flip_Flop d_ff_3 (.D(SHIFT_REGISTER), .clk(in_2), .Q(out_5));  // open: Qn, preset, reset
  D_Flip_Flop d_ff_4 (.D(out_5), .clk(in_1), .Q(out_6));  // open: Qn, preset, reset

  // Notes on the sheet:
  //   D Flip-Flop
  //   Reset the simulation, put positive edge clock alternately
endmodule
